# Fritzing sketch AndromedaDress_Wiring (saved by Fritzing 0.9.2b)

parts:
  BATT1 = 3xAAA Switchable Battery Pack w/Bare Wire  # not connected
  FLORA1 = Adafruit_Flora
  10_0 = Adafruit_FLORA_RGB_Smart_Pixel
  10_1 = Adafruit_FLORA_RGB_Smart_Pixel
  10_2 = Adafruit_FLORA_RGB_Smart_Pixel
  10_3 = Adafruit_FLORA_RGB_Smart_Pixel
  10_4 = Adafruit_FLORA_RGB_Smart_Pixel
  6_0 = Adafruit_FLORA_RGB_Smart_Pixel
  6_1 = Adafruit_FLORA_RGB_Smart_Pixel
  6_2 = Adafruit_FLORA_RGB_Smart_Pixel
  6_3 = Adafruit_FLORA_RGB_Smart_Pixel
  6_4 = Adafruit_FLORA_RGB_Smart_Pixel
  6_5 = Adafruit_FLORA_RGB_Smart_Pixel
  6_6 = Adafruit_FLORA_RGB_Smart_Pixel
  6_7 = Adafruit_FLORA_RGB_Smart_Pixel
  9_0 = Adafruit_FLORA_RGB_Smart_Pixel
  9_1 = Adafruit_FLORA_RGB_Smart_Pixel
  9_2 = Adafruit_FLORA_RGB_Smart_Pixel

nets:
  N1: FLORA1.connector1, 10_0.connector3, 10_1.connector3, 10_2.connector3, 10_3.connector3, 10_4.connector3, 6_0.connector3, 6_1.connector3, 6_2.connector3, 6_3.connector3, 6_4.connector3, 6_5.connector3, 6_6.connector3, 6_7.connector3, 9_0.connector3, 9_1.connector3, 9_2.connector3
  N2: FLORA1.connector8, 10_0.connector1, 10_1.connector1, 10_2.connector1, 10_3.connector1, 10_4.connector1, 6_0.connector1, 6_1.connector1, 6_2.connector1, 6_3.connector1, 6_4.connector1, 6_5.connector1, 6_6.connector1, 6_7.connector1, 9_0.connector1, 9_1.connector1, 9_2.connector1
  N3: FLORA1.connector10, 6_0.connector2
  N4: FLORA1.connector12, 9_0.connector2
  N5: FLORA1.connector13, 10_0.connector2
  N6: 10_0.connector4, 10_1.connector2
  N7: 10_1.connector4, 10_2.connector2
  N8: 10_2.connector4, 10_3.connector2
  N9: 10_3.connector4, 10_4.connector2
  N10: 6_0.connector4, 6_1.connector2
  N11: 6_1.connector4, 6_2.connector2
  N12: 6_2.connector4, 6_3.connector2
  N13: 6_3.connector4, 6_4.connector2
  N14: 6_4.connector4, 6_5.connector2
  N15: 6_5.connector4, 6_6.connector2
  N16: 6_6.connector4, 6_7.connector2
  N17: 9_0.connector4, 9_1.connector2
  N18: 9_1.connector4, 9_2.connector2

custom parts:
  3xAAA Switchable Battery Pack w/Bare Wire: 3xAAA Switchable Battery Pack w/Bare Wire Connectors
